// Logisim project finalFinalGCD.circ as structural Verilog: 1 circuit, main circuit main
module main (
  input  [31:0] in_1,
  input  [31:0] in_2,
  input  in_3
);

  wire and_1_out, and_2_out, and_3_out, and_4_out, and_5_out, and_6_out, clock_1_out, comparator_1_eq,
       comparator_1_gt, comparator_1_lt, d_ff_1_qn, d_ff_2_qn, d_ff_3_qn, decoder_1_out1, decoder_1_out3,
       decoder_1_out4, decoder_1_out5, not_1_out, or_1_out, or_2_out, or_3_out, or_4_out, or_5_out;
  wire [2:0] d_ff_1_q;
  wire [31:0] multiplexer_1_out, multiplexer_2_out, register_1_q, register_3_q, subtractor_1_out,
       subtractor_2_out;

  Clock clock_1 (.out(clock_1_out));
  and and_1 (and_1_out, d_ff_1_qn, d_ff_1_q[1], or_1_out);
  Multiplexer #(.width(32), .enable("false")) multiplexer_1 (
    .in0(in_1), .in1(subtractor_1_out), .out(multiplexer_1_out), .sel(decoder_1_out3));
  Register #(.width(32)) register_1 (
    .D(multiplexer_1_out), .en(or_4_out), .Q(register_1_q), .clk(clock_1_out));  // open: clr
  Comparator #(.width(32)) comparator_1 (
    .a(register_1_q), .b(register_3_q), .gt(comparator_1_gt), .eq(comparator_1_eq), .lt(comparator_1_lt));
  or or_1 (or_1_out, comparator_1_lt, comparator_1_eq);
  not not_1 (not_1_out, comparator_1_lt);
  and and_2 (and_2_out, not_1_out, d_ff_1_q[1], d_ff_1_qn);
  or or_2 (or_2_out, and_2_out, and_3_out);
  Subtractor #(.width(32)) subtractor_1 (
    .a(register_1_q), .b(register_3_q), .out(subtractor_1_out));  // open: bin, bout
  Register #(.width(32)) register_2 (.D(register_1_q), .en(decoder_1_out5), .clk(clock_1_out));  // open: Q, clr
  Multiplexer #(.width(32), .enable("false")) multiplexer_2 (
    .in0(in_2), .in1(subtractor_2_out), .out(multiplexer_2_out), .sel(decoder_1_out4));
  and and_3 (and_3_out, in_3, d_ff_1_qn, d_ff_2_qn, d_ff_3_qn);
  Register #(.width(32)) register_3 (
    .D(multiplexer_2_out), .en(or_5_out), .Q(register_3_q), .clk(clock_1_out));  // open: clr
  Subtractor #(.width(32)) subtractor_2 (
    .a(register_3_q), .b(register_1_q), .out(subtractor_2_out));  // open: bin, bout
  and and_4 (and_4_out, comparator_1_gt, d_ff_1_q[1], d_ff_1_qn);
  and and_5 (and_5_out, d_ff_1_q[2], d_ff_1_qn);
  or or_3 (or_3_out, and_4_out, and_5_out, and_6_out);
  D_Flip_Flop d_ff_1 (.clk(clock_1_out), .D(or_2_out), .Q(d_ff_1_q[0]), .Qn(d_ff_1_qn));  // open: preset, en, reset
  D_Flip_Flop d_ff_2 (.clk(clock_1_out), .D(or_3_out), .Q(d_ff_1_q[1]), .Qn(d_ff_2_qn));  // open: preset, en, reset
  D_Flip_Flop d_ff_3 (.clk(clock_1_out), .D(and_1_out), .Q(d_ff_1_q[2]), .Qn(d_ff_3_qn));  // open: preset, en, reset
  and and_6 (and_6_out, d_ff_3_qn, d_ff_1_q[0]);
  Decoder #(.select(3), .enable("false")) decoder_1 (
    .out1(decoder_1_out1), .out3(decoder_1_out3), .out4(decoder_1_out4), .out5(decoder_1_out5), .sel(d_ff_1_q));  // open: out0, out2, out6, out7
  or or_4 (or_4_out, decoder_1_out1, decoder_1_out3);
  or or_5 (or_5_out, decoder_1_out1, decoder_1_out4);

  // Notes on the sheet:
  //   INPUT X
  //   x register
  //   g,e,l
  //   output d
  //   x-y
  //   y register
  //   y-x
  //   INPUT Y
  //   CONTROL Unit
  //   0
  //   1
  //   2
endmodule
