// Logisim project final.circ as structural Verilog: 4 circuits, main circuit main
module main (
  input  go
);

  wire adder_1_p3, and_1_out, and_2_out, and_3_out, and_4_out, clock_1_out, comparator_1_p1, comparator_1_p2,
       comparator_2_p1, comparator_2_p2, comparator_3_p1, comparator_3_p2, comparator_4_p2, comparator_4_p3,
       comparator_4_p4, comparator_5_p1, comparator_5_p2, comparator_5_p3, comparator_6_p1, comparator_6_p2,
       decoder_1_out1, decoder_2_out2, decoder_2_out3, decoder_2_out5, decoder_2_out7, decoder_2_out8,
       fp_const_5_p1, fp_const_6_p1, or_1_out, or_2_out, or_3_out, or_5_out, or_6_out, or_7_out, or_8_out,
       subtractor_1_p3, subtractor_1_p4;
  wire [3:0] controlunit_1_d0;
  wire [31:0] controlfunc_1_out, controlfunc_2_out, controlfunc_3_out, controlfunc_4_out, controlfunc_5_out,
       demultiplexer_1_out0, demultiplexer_1_out1, divider_1_p3, fp_const_1_p1, fp_const_8_p1,
       fp_const_10_p1, fp_const_11_p1, fp_const_12_p1, fp_const_13_p1, fp_const_14_p1, fp_probe_1_p1,
       fp_probe_6_p1, multiplexer_1_out, multiplexer_2_out, multiplexer_3_out, register_1_q, register_3_q;

  Clock clock_1 (.out(clock_1_out));
  // FP_Const fp_const_1: pin names not known; wires that end beside it: fp_const_1_p1
  controlfunc controlfunc_1 (
    .a(fp_const_10_p1), .x(register_1_q), .d(fp_const_13_p1), .c(fp_const_12_p1), .b(fp_const_11_p1),
    .e(fp_const_14_p1), .out(controlfunc_1_out));
  controlfunc controlfunc_2 (
    .a(fp_const_10_p1), .x(register_3_q), .d(fp_const_13_p1), .c(fp_const_12_p1), .b(fp_const_11_p1),
    .e(fp_const_14_p1), .out(controlfunc_2_out));
  // FP_Const fp_const_2: pin names not known; wires that end beside it: controlfunc_2_out
  controlfunc controlfunc_3 (
    .a(fp_const_10_p1), .x(fp_const_1_p1), .d(fp_const_13_p1), .c(fp_const_12_p1), .b(fp_const_11_p1),
    .e(fp_const_14_p1), .out(controlfunc_3_out));
  Register #(.width(32)) register_1 (
    .D(multiplexer_1_out), .en(or_8_out), .Q(register_1_q), .clk(clock_1_out));  // open: clr
  Multiplexer #(.width(32), .enable("false")) multiplexer_1 (
    .in0(fp_const_1_p1), .in1(demultiplexer_1_out0), .out(multiplexer_1_out), .sel(decoder_2_out8));
  // Comparator comparator_1: pin names not known; wires that end beside it: comparator_1_p1, comparator_1_p2
  // FP_Const fp_const_3: pin names not known; wires that end beside it: controlfunc_1_out
  // Comparator comparator_2: pin names not known; wires that end beside it: comparator_2_p1, comparator_2_p2
  and and_1 (and_1_out, comparator_1_p1, comparator_2_p2);
  // Comparator comparator_3: pin names not known; wires that end beside it: comparator_3_p1, comparator_3_p2
  // FP_Const fp_const_4: pin names not known; wires that end beside it: controlfunc_3_out
  Demultiplexer #(.width(32), .enable("false")) demultiplexer_1 (
    .out0(demultiplexer_1_out0), .out1(demultiplexer_1_out1), .in(register_3_q), .sel(or_1_out));
  and and_2 (and_2_out, comparator_2_p1, comparator_1_p2);
  or or_1 (or_1_out, and_2_out, and_1_out);
  and and_3 (and_3_out, comparator_3_p1, comparator_6_p2);
  // FP_Probe fp_probe_1: pin names not known; wires that end beside it: fp_probe_1_p1
  Multiplexer #(.width(32), .enable("false")) multiplexer_2 (
    .in0(fp_const_8_p1), .in1(demultiplexer_1_out1), .out(multiplexer_2_out), .sel(decoder_2_out7));
  // Subtractor subtractor_1: pin names not known; wires that end beside it: fp_probe_1_p1, register_1_q, subtractor_1_p3, subtractor_1_p4
  // FP_Probe fp_probe_2: pin names not known; wires that end beside it: controlfunc_3_out
  and and_4 (and_4_out, comparator_3_p2, comparator_6_p1);
  or or_2 (or_2_out, and_3_out, and_4_out);
  Decoder #(.enable("false")) decoder_1 (.out1(decoder_1_out1), .sel(or_2_out));  // open: out0
  Register #(.width(32)) register_2 (
    .D(multiplexer_2_out), .en(or_7_out), .Q(fp_probe_1_p1), .clk(clock_1_out));  // open: clr
  // Comparator comparator_4: pin names not known; wires that end beside it: subtractor_1_p4, comparator_4_p2, comparator_4_p3, comparator_4_p4
  // FP_Const fp_const_5: pin names not known; wires that end beside it: fp_const_5_p1, subtractor_1_p3, fp_const_5_p1
  controlfunc controlfunc_4 (
    .a(fp_const_10_p1), .x(register_3_q), .d(fp_const_13_p1), .c(fp_const_12_p1), .b(fp_const_11_p1),
    .e(fp_const_14_p1), .out(controlfunc_4_out));
  LED led_1 (.in(decoder_2_out2));
  // Adder adder_1: pin names not known; wires that end beside it: register_1_q, fp_probe_1_p1, adder_1_p3
  // FP_Const fp_const_6: pin names not known; wires that end beside it: fp_const_6_p1
  // FP_Probe fp_probe_3: pin names not known
  or or_3 (or_3_out, comparator_4_p3, comparator_4_p4);
  // Comparator comparator_5: pin names not known; wires that end beside it: comparator_5_p1, comparator_5_p2, comparator_5_p3
  // FP_Const fp_const_7: pin names not known; wires that end beside it: controlfunc_4_out
  controlfunc controlfunc_5 (
    .a(fp_const_10_p1), .x(fp_const_8_p1), .d(fp_const_13_p1), .c(fp_const_12_p1), .b(fp_const_11_p1),
    .e(fp_const_14_p1), .out(controlfunc_5_out));
  Multiplexer #(.width(32), .enable("false")) multiplexer_3 (
    .in0(fp_const_1_p1), .in1(divider_1_p3), .out(multiplexer_3_out), .sel(decoder_2_out5));
  // Divider divider_1: pin names not known; wires that end beside it: adder_1_p3, fp_const_6_p1, divider_1_p3
  // FP_Const fp_const_8: pin names not known; wires that end beside it: fp_const_8_p1, controlfunc_5_out
  // FP_Const fp_const_9: pin names not known; wires that end beside it: controlfunc_5_out
  Register #(.width(32)) register_3 (
    .D(multiplexer_3_out), .en(or_6_out), .Q(register_3_q), .clk(clock_1_out));  // open: clr
  // OR_Gate or_4 has open pins: in0=comparator_5_p1, in1=comparator_5_p3, out=open
  // Comparator comparator_6: pin names not known; wires that end beside it: comparator_6_p1, comparator_6_p2
  LED led_2 (.in(or_5_out));
  LED led_3 (.in(or_5_out));
  LED led_4 (.in(or_5_out));
  LED led_5 (.in(or_5_out));
  or or_5 (or_5_out, comparator_4_p2, comparator_5_p2);
  // FP_Probe fp_probe_4: pin names not known
  // FP_Probe fp_probe_5: pin names not known; wires that end beside it: register_3_q
  LED led_6 (.in(or_5_out));
  // FP_Probe fp_probe_6: pin names not known; wires that end beside it: fp_probe_6_p1, or_5_out
  Multiplexer #(.width(32), .enable("false")) multiplexer_4 (
    .in1(register_3_q), .out(fp_probe_6_p1), .sel(or_5_out));  // open: in0
  controlunit controlunit_1 (
    .go(go), .bas(decoder_1_out1), .beps(or_3_out), .func(comparator_5_p2), .d0(controlunit_1_d0[0]),
    .ac(or_1_out), .d1(controlunit_1_d0[1]), .d3(controlunit_1_d0[3]), .d2(controlunit_1_d0[2]));
  // FP_Const fp_const_10: pin names not known; wires that end beside it: fp_const_10_p1
  // FP_Const fp_const_11: pin names not known; wires that end beside it: fp_const_11_p1
  // FP_Const fp_const_12: pin names not known; wires that end beside it: fp_const_12_p1
  // FP_Const fp_const_13: pin names not known; wires that end beside it: fp_const_13_p1
  // FP_Const fp_const_14: pin names not known; wires that end beside it: fp_const_14_p1
  or or_6 (or_6_out, decoder_2_out3, decoder_2_out5);
  Decoder #(.select(4), .enable("false")) decoder_2 (
    .out2(decoder_2_out2), .out3(decoder_2_out3), .out5(decoder_2_out5), .out7(decoder_2_out7),
    .out8(decoder_2_out8), .sel(controlunit_1_d0));  // open: out0, out1, out4, out6, out9, out10, out11, out12, out13, out14, out15
  or or_7 (or_7_out, decoder_2_out3, decoder_2_out7);
  or or_8 (or_8_out, decoder_2_out3, decoder_2_out8);

  // Notes on the sheet:
  //   INPUT A
  //   else if(func * funca <0)
  //   a
  //   a1 = c atanması
  //   abcde
  //   sayilari carpmadan isaretlerini and/orla carpimlari ne olacak bul
  //   b1=c atanması
  //   b
  //   b1-a1>=epsilon
  //   if(func)=0
  //   INPUT B
  //   Bu isik yaniyorsa fail , tekrar input veriniz
  //   c=(a+b)/2
  //   c
  //   SONUC
  //   a
  //   b
  //   c
  //   d
  //   e
  //   ax4+bx3+cx2+dx+e
  //   sonuc yokken NAN/err versin
endmodule

module func (
  input  [31:0] in_1,
  output [31:0] out_2
);

  wire fp_const_1_p1, multiplier_1_p3, multiplier_2_p3, subtractor_1_p3;

  // Multiplier multiplier_1: pin names not known; wires that end beside it: in_1, in_1, multiplier_1_p3
  // FP_Probe fp_probe_1: pin names not known; wires that end beside it: multiplier_1_p3
  // Multiplier multiplier_2: pin names not known; wires that end beside it: multiplier_1_p3, in_1, multiplier_2_p3
  // FP_Const fp_const_1: pin names not known; wires that end beside it: fp_const_1_p1
  // FP_Probe fp_probe_2: pin names not known; wires that end beside it: multiplier_2_p3
  // Subtractor subtractor_1: pin names not known; wires that end beside it: multiplier_2_p3, multiplier_1_p3, subtractor_1_p3
  // Adder adder_1: pin names not known; wires that end beside it: subtractor_1_p3, fp_const_1_p1, out_2
  // FP_Probe fp_probe_3: pin names not known; wires that end beside it: subtractor_1_p3
  // FP_Probe fp_probe_4: pin names not known

  // Notes on the sheet:
  //   INPUT A
  //   x3-x2+2 func 
  //   x2
  //   x3
  //   x3-x2
endmodule

module controlunit (
  input  go,
  input  bas,
  input  beps,
  input  func,
  input  ac,
  output d3,
  output d2,
  output d1,
  output d0
);

  wire and_1_out, and_2_out, and_3_out, and_4_out, and_5_out, and_6_out, and_7_out, and_8_out, and_9_out,
       and_10_out, and_11_out, and_12_out, and_13_out, and_14_out, and_15_out, and_16_out, and_17_out,
       clock_1_out, d0_qn, d3_qn, d_ff_1_qn, d_ff_2_qn, not_1_out, not_2_out, not_3_out, not_4_out,
       not_6_out, not_7_out, not_8_out, not_9_out, not_10_out, or_1_out, or_2_out, or_3_out, or_4_out;

  Clock clock_1 (.out(clock_1_out));
  not not_1 (not_1_out, beps);
  not not_2 (not_2_out, ac);
  not not_3 (not_3_out, func);
  not not_4 (not_4_out, d0_qn);
  D_Flip_Flop u_d3 (.clk(clock_1_out), .D(or_1_out), .Q(d3), .Qn(d3_qn));  // open: preset, en, reset
  and and_1 (and_1_out, d3_qn, d_ff_1_qn, go, d_ff_2_qn, d0_qn);
  D_Flip_Flop d_ff_1 (.clk(clock_1_out), .D(or_2_out), .Q(d2), .Qn(d_ff_1_qn));  // open: preset, en, reset
  D_Flip_Flop d_ff_2 (.clk(clock_1_out), .D(or_3_out), .Q(d1), .Qn(d_ff_2_qn));  // open: preset, en, reset
  D_Flip_Flop u_d0 (.clk(clock_1_out), .D(or_4_out), .Q(d0), .Qn(d0_qn));  // open: preset, en, reset
  and and_2 (and_2_out, d3_qn, d_ff_1_qn, d_ff_2_qn, d0);
  and and_3 (and_3_out, d3_qn, d2, d_ff_2_qn, d0_qn, not_1_out);
  and and_4 (and_4_out, d3_qn, d2, d_ff_2_qn, d0, func);
  and and_5 (and_5_out, d3_qn, d2, d_ff_2_qn, d0, not_3_out);
  and and_6 (and_6_out, d3_qn, d_ff_1_qn, d_ff_2_qn, not_4_out, bas);
  and and_7 (and_7_out, d3_qn, d2, d1, d0_qn, not_2_out);
  or or_1 (or_1_out, and_3_out, and_4_out, and_7_out);
  and and_8 (and_8_out, d3_qn, d_ff_1_qn, d1, d0);
  and and_9 (and_9_out, d3_qn, d2, d1, d0_qn, ac);
  and and_10 (and_10_out, d3_qn, d2, d_ff_2_qn, d0_qn);
  // NOT_Gate not_5 has open pins: in=d3_qn, out=open
  and and_11 (and_11_out, d3_qn, d2, d_ff_2_qn, d0_qn, bas);
  and and_12 (and_12_out, d3_qn, d2, d_ff_2_qn, d0, not_3_out);
  or or_2 (or_2_out, and_8_out, and_11_out, and_12_out, and_13_out, and_15_out, and_17_out);
  and and_13 (and_13_out, d3_qn, d2, d1, d0_qn, ac);
  and and_14 (and_14_out, d3_qn, d2, d_ff_2_qn, not_4_out, func);
  not not_6 (not_6_out, d_ff_2_qn);
  or or_3 (or_3_out, and_9_out, and_5_out, and_2_out);
  not not_7 (not_7_out, d3_qn);
  not not_8 (not_8_out, d2);
  not not_9 (not_9_out, d1);
  and and_15 (and_15_out, d3_qn, d2, d1, d0);
  and and_16 (and_16_out, d3_qn, d2, not_6_out, d0_qn, ac);
  not not_10 (not_10_out, d0);
  and and_17 (and_17_out, not_7_out, not_8_out, not_9_out, not_10_out);
  or or_4 (or_4_out, and_1_out, and_6_out, and_10_out, and_14_out, and_16_out);

  // Notes on the sheet:
  //   !d0 d0
  //   N1
  //   !d1 d1
  //   n3
  //   !d1 d2
  //   2
  //   !d3 d3
  //   n2
endmodule

module controlfunc (
  input  [31:0] e,
  input  [31:0] a,
  input  [31:0] x,
  input  [31:0] d,
  input  [31:0] c,
  input  [31:0] b,
  output [31:0] out
);

  wire adder_1_p3, adder_2_p3, adder_3_p3, multiplier_1_p3, multiplier_2_p1, multiplier_2_p3,
       multiplier_3_p1, multiplier_5_p2, multiplier_5_p3, multiplier_7_p3;

  // Multiplier multiplier_1: pin names not known; wires that end beside it: x, d, multiplier_1_p3
  // Multiplier multiplier_2: pin names not known; wires that end beside it: multiplier_2_p1, b, multiplier_2_p3
  // Multiplier multiplier_3: pin names not known; wires that end beside it: multiplier_3_p1, x, multiplier_2_p1
  // Multiplier multiplier_4: pin names not known; wires that end beside it: x, x, multiplier_3_p1
  // Multiplier multiplier_5: pin names not known; wires that end beside it: a, multiplier_5_p2, multiplier_5_p3
  // Multiplier multiplier_6: pin names not known; wires that end beside it: multiplier_3_p1, multiplier_3_p1, multiplier_5_p2
  // Multiplier multiplier_7: pin names not known; wires that end beside it: c, multiplier_3_p1, multiplier_7_p3
  // Adder adder_1: pin names not known; wires that end beside it: multiplier_7_p3, multiplier_1_p3, adder_1_p3
  // Adder adder_2: pin names not known; wires that end beside it: multiplier_5_p3, multiplier_2_p3, adder_2_p3
  // Adder adder_3: pin names not known; wires that end beside it: adder_2_p3, adder_1_p3, adder_3_p3
  // Adder adder_4: pin names not known; wires that end beside it: e, adder_3_p3, out

  // Notes on the sheet:
  //   dx
  //   bx3
  //   INPUT A
  //   ax4+bx3+cx2+dx+ex
  //   ax4
  //   cx2
endmodule
